// Logisim project DataMemory.circ as structural Verilog: 1 circuit, main circuit main
module main (
  input  [31:0] in_1,
  input  MemWrite,
  input  Clock,
  input  MemRead,
  output [31:0] Address_Read
);

  RAM #(.addrWidth(24), .dataWidth(32), .bus("separate")) ram_1 (
    .addr(in_1[23:0]), .data(Address_Read), .str(MemWrite), .clk(Clock), .ld(MemRead));  // open: din, sel, clr
endmodule
