// Logisim project adder.circ as structural Verilog: 3 circuits, main circuit main
module main (
  input  [31:0] in_1,
  input  [31:0] in_2,
  output [31:0] out_3
);

  or or_1 (out_3[0], in_1[0], in_2[0]);
  or or_2 (out_3[1], in_1[1], in_2[1]);
  or or_3 (out_3[2], in_1[2], in_2[2]);
  or or_4 (out_3[3], in_1[3], in_2[3]);
  or or_5 (out_3[4], in_1[4], in_2[4]);
  or or_6 (out_3[5], in_1[5], in_2[5]);
  or or_7 (out_3[6], in_1[6], in_2[6]);
  or or_8 (out_3[7], in_1[7], in_2[7]);
  or or_9 (out_3[8], in_1[8], in_2[8]);
  or or_10 (out_3[9], in_1[9], in_2[9]);
  or or_11 (out_3[10], in_1[10], in_2[10]);
  or or_12 (out_3[11], in_1[11], in_2[11]);
  or or_13 (out_3[12], in_1[12], in_2[12]);
  or or_14 (out_3[13], in_1[13], in_2[13]);
  or or_15 (out_3[14], in_1[14], in_2[14]);
  or or_16 (out_3[15], in_1[15], in_2[15]);
  or or_17 (out_3[16], in_1[16], in_2[16]);
  or or_18 (out_3[17], in_1[17], in_2[17]);
  or or_19 (out_3[18], in_1[18], in_2[18]);
  or or_20 (out_3[19], in_1[19], in_2[19]);
  or or_21 (out_3[20], in_1[20], in_2[20]);
  or or_22 (out_3[21], in_1[21], in_2[21]);
  or or_23 (out_3[22], in_1[22], in_2[22]);
  or or_24 (out_3[23], in_1[23], in_2[23]);
  or or_25 (out_3[24], in_1[24], in_2[24]);
  or or_26 (out_3[25], in_1[25], in_2[25]);
  or or_27 (out_3[26], in_1[26], in_2[26]);
  or or_28 (out_3[27], in_1[27], in_2[27]);
  or or_29 (out_3[28], in_1[28], in_2[28]);
  or or_30 (out_3[29], in_1[29], in_2[29]);
  or or_31 (out_3[30], in_1[30], in_2[30]);
  or or_32 (out_3[31], in_1[31], in_2[31]);

  // Notes on the sheet:
  //   A
  //   1
  //   5
  //   10
  //   15
  //   20
  //   25
  //   B
endmodule

module _32_bit_And_Gate (
  input  [31:0] in_1,
  input  [31:0] in_2,
  output [31:0] out_3
);

  or or_1 (out_3[0], in_1[0], in_2[0]);
  or or_2 (out_3[1], in_1[1], in_2[1]);
  or or_3 (out_3[2], in_1[2], in_2[2]);
  or or_4 (out_3[3], in_1[3], in_2[3]);
  or or_5 (out_3[4], in_1[4], in_2[4]);
  or or_6 (out_3[5], in_1[5], in_2[5]);
  or or_7 (out_3[6], in_1[6], in_2[6]);
  or or_8 (out_3[7], in_1[7], in_2[7]);
  or or_9 (out_3[8], in_1[8], in_2[8]);
  or or_10 (out_3[9], in_1[9], in_2[9]);
  or or_11 (out_3[10], in_1[10], in_2[10]);
  or or_12 (out_3[11], in_1[11], in_2[11]);
  or or_13 (out_3[12], in_1[12], in_2[12]);
  or or_14 (out_3[13], in_1[13], in_2[13]);
  or or_15 (out_3[14], in_1[14], in_2[14]);
  or or_16 (out_3[15], in_1[15], in_2[15]);
  or or_17 (out_3[16], in_1[16], in_2[16]);
  or or_18 (out_3[17], in_1[17], in_2[17]);
  or or_19 (out_3[18], in_1[18], in_2[18]);
  or or_20 (out_3[19], in_1[19], in_2[19]);
  or or_21 (out_3[20], in_1[20], in_2[20]);
  or or_22 (out_3[21], in_1[21], in_2[21]);
  or or_23 (out_3[22], in_1[22], in_2[22]);
  or or_24 (out_3[23], in_1[23], in_2[23]);
  or or_25 (out_3[24], in_1[24], in_2[24]);
  or or_26 (out_3[25], in_1[25], in_2[25]);
  or or_27 (out_3[26], in_1[26], in_2[26]);
  or or_28 (out_3[27], in_1[27], in_2[27]);
  or or_29 (out_3[28], in_1[28], in_2[28]);
  or or_30 (out_3[29], in_1[29], in_2[29]);
  or or_31 (out_3[30], in_1[30], in_2[30]);
  or or_32 (out_3[31], in_1[31], in_2[31]);

  // Notes on the sheet:
  //   1
  //   5
  //   10
  //   15
  //   20
  //   25
  //   B
endmodule

module Adder_Subtractor (
  input  in_1,
  input  [31:0] in_2,
  input  [31:0] in_3
);

  wire adder_1_cout, adder_2_cout, adder_3_cout, adder_4_cout, adder_5_cout, adder_6_cout, adder_7_cout,
       adder_8_cout, adder_9_cout, adder_10_cout, adder_11_cout, adder_12_cout, adder_13_cout, adder_14_cout,
       adder_15_cout, adder_16_cout, adder_17_cout, adder_18_cout, adder_19_cout, adder_20_cout,
       adder_21_cout, adder_23_cout, adder_24_cout, adder_25_cout, adder_26_cout, adder_27_cout,
       adder_28_cout, adder_29_cout, adder_30_cout, adder_31_cout, xor_1_out, xor_2_out, xor_3_out;
  wire [7:0] adder_28_out;

  xor xor_1 (xor_1_out, in_2[0], in_1);
  xor xor_2 (xor_2_out, in_2[1], in_1);
  xor xor_3 (xor_3_out, in_2[2], in_1);
  // XOR_Gate xor_4 has open pins: in0=in_2[3], in1=in_1, out=open
  // XOR_Gate xor_5 has open pins: in0=in_2[4], in1=in_1, out=open
  // XOR_Gate xor_6 has open pins: in0=in_2[5], in1=in_1, out=open
  // XOR_Gate xor_7 has open pins: in0=in_2[6], in1=in_1, out=open
  // XOR_Gate xor_8 has open pins: in0=in_2[7], in1=in_1, out=open
  // XOR_Gate xor_9 has open pins: in0=in_2[8], in1=in_1, out=open
  // XOR_Gate xor_10 has open pins: in0=in_2[9], in1=in_1, out=open
  // XOR_Gate xor_11 has open pins: in0=in_2[10], in1=in_1, out=open
  // XOR_Gate xor_12 has open pins: in0=in_2[11], in1=in_1, out=open
  // XOR_Gate xor_13 has open pins: in0=in_2[12], in1=in_1, out=open
  // XOR_Gate xor_14 has open pins: in0=in_2[13], in1=in_1, out=open
  // XOR_Gate xor_15 has open pins: in0=in_2[14], in1=in_1, out=open
  // XOR_Gate xor_16 has open pins: in0=in_2[15], in1=in_1, out=open
  // XOR_Gate xor_17 has open pins: in0=in_2[16], in1=in_1, out=open
  // XOR_Gate xor_18 has open pins: in0=in_2[17], in1=in_1, out=open
  // XOR_Gate xor_19 has open pins: in0=in_2[18], in1=in_1, out=open
  // XOR_Gate xor_20 has open pins: in0=in_2[19], in1=in_1, out=open
  // XOR_Gate xor_21 has open pins: in0=in_2[20], in1=in_1, out=open
  // XOR_Gate xor_22 has open pins: in0=in_2[21], in1=in_1, out=open
  // XOR_Gate xor_23 has open pins: in0=in_2[22], in1=in_1, out=open
  // XOR_Gate xor_24 has open pins: in0=in_2[23], in1=in_1, out=open
  // XOR_Gate xor_25 has open pins: in0=in_2[24], in1=in_1, out=open
  // XOR_Gate xor_26 has open pins: in0=in_2[25], in1=in_1, out=open
  // XOR_Gate xor_27 has open pins: in0=in_2[26], in1=in_1, out=open
  // XOR_Gate xor_28 has open pins: in0=in_2[27], in1=in_1, out=open
  // XOR_Gate xor_29 has open pins: in0=in_2[28], in1=in_1, out=open
  // XOR_Gate xor_30 has open pins: in0=in_2[29], in1=in_1, out=open
  // XOR_Gate xor_31 has open pins: in0=in_2[30], in1=in_1, out=open
  // XOR_Gate xor_32 has open pins: in0=in_2[31], in1=in_1, out=open
  Adder #(.width(1)) adder_1 (.b(xor_1_out), .cin(in_1), .cout(adder_1_cout));  // open: a, out
  Adder #(.width(1)) adder_2 (.b(xor_2_out), .cin(adder_1_cout), .cout(adder_2_cout));  // open: a, out
  Adder #(.width(1)) adder_3 (.b(xor_3_out), .cin(adder_2_cout), .cout(adder_3_cout));  // open: a, out
  Adder adder_4 (.cin(adder_3_cout), .cout(adder_4_cout));  // open: a, b, out
  Adder #(.width(1)) adder_5 (.cin(adder_4_cout), .cout(adder_5_cout));  // open: a, b, out
  Adder adder_6 (.cin(adder_5_cout), .cout(adder_6_cout));  // open: a, b, out
  Adder adder_7 (.cin(adder_6_cout), .cout(adder_7_cout));  // open: a, b, out
  Adder adder_8 (.cin(adder_7_cout), .cout(adder_8_cout));  // open: a, b, out
  Adder #(.width(1)) adder_9 (.cin(adder_8_cout), .cout(adder_9_cout));  // open: a, b, out
  Adder adder_10 (.cin(adder_9_cout), .cout(adder_10_cout));  // open: a, b, out
  Adder adder_11 (.cin(adder_10_cout), .cout(adder_11_cout));  // open: a, b, out
  Adder adder_12 (.cin(adder_11_cout), .cout(adder_12_cout));  // open: a, b, out
  Adder #(.width(1)) adder_13 (.cin(adder_12_cout), .cout(adder_13_cout));  // open: a, b, out
  Adder adder_14 (.cin(adder_13_cout), .cout(adder_14_cout));  // open: a, b, out
  Adder adder_15 (.cin(adder_14_cout), .cout(adder_15_cout));  // open: a, b, out
  Adder adder_16 (.cin(adder_15_cout), .cout(adder_16_cout));  // open: a, b, out
  Adder #(.width(1)) adder_17 (.cin(adder_16_cout), .cout(adder_17_cout));  // open: a, b, out
  Adder adder_18 (.cin(adder_17_cout), .cout(adder_18_cout));  // open: a, b, out
  Adder adder_19 (.cin(adder_18_cout), .cout(adder_19_cout));  // open: a, b, out
  Adder adder_20 (.cin(adder_19_cout), .cout(adder_20_cout));  // open: a, b, out
  Adder #(.width(1)) adder_21 (.cin(adder_20_cout), .cout(adder_21_cout));  // open: a, b, out
  Adder adder_22 (.cin(adder_21_cout));  // open: a, b, out, cout
  Adder adder_23 (.cout(adder_23_cout));  // open: a, b, out, cin
  Adder adder_24 (.cin(adder_23_cout), .cout(adder_24_cout));  // open: a, b, out
  Adder #(.width(1)) adder_25 (.cin(adder_24_cout), .cout(adder_25_cout));  // open: a, b, out
  Adder adder_26 (.cin(adder_25_cout), .cout(adder_26_cout));  // open: a, b, out
  Adder adder_27 (.cin(adder_26_cout), .cout(adder_27_cout));  // open: a, b, out
  Adder adder_28 (.out(adder_28_out), .cin(adder_27_cout), .cout(adder_28_cout));  // open: a, b
  Adder #(.width(1)) adder_29 (.cin(adder_28_cout), .cout(adder_29_cout));  // open: a, b, out
  Adder adder_30 (.cin(adder_29_cout), .cout(adder_30_cout));  // open: a, b, out
  Adder adder_31 (.cin(adder_30_cout), .cout(adder_31_cout));  // open: a, b, out
  Adder adder_32 (.cin(adder_31_cout));  // open: a, b, out, cout

  // Notes on the sheet:
  //   A
  //   4
  //   8
  //   12
  //   16
  //   20
  //   24
  //   28
  //   4
  //   8
  //   12
  //   16
  //   20
endmodule
