// Logisim project shifter.circ as structural Verilog: 1 circuit, main circuit main
module main (
  input  [4:0] ShiftAmt,
  input  [31:0] Input,
  input  [1:0] Input_2,
  output [31:0] out_4
);

  wire [31:0] shifter_1_out, shifter_2_out, shifter_3_out;

  Shifter #(.width(32)) shifter_1 (.in(Input), .\dist (ShiftAmt), .out(shifter_1_out));
  Shifter #(.width(32), .shift("lr")) shifter_2 (.in(Input), .\dist (ShiftAmt), .out(shifter_2_out));
  Shifter #(.width(32), .shift("ar")) shifter_3 (.in(Input), .\dist (ShiftAmt), .out(shifter_3_out));
  Multiplexer #(.select(2), .width(32)) multiplexer_1 (
    .in1(shifter_1_out), .in2(shifter_2_out), .in3(shifter_3_out), .out(out_4), .sel(Input_2));  // open: in0, en
endmodule
